// Logisim project TuringComplete.circ as structural Verilog: 16 circuits, main circuit main
module main (
  input  Reset,
  input  [7:0] in_2,
  input  [7:0] in_3,
  input  [7:0] in_4,
  input  in_5,
  output [7:0] Reg0,
  output [7:0] Reg1,
  output [7:0] Reg2,
  output [7:0] Reg3,
  output [7:0] Reg4,
  output [7:0] Reg5,
  output [7:0] out_12,
  output [7:0] Reg6,
  output [63:0] out_14,
  output [63:0] out_15,
  output [63:0] out_16,
  output [63:0] out_17,
  output [63:0] out_18,
  output [63:0] out_19,
  output [63:0] out_20,
  output [63:0] out_21,
  output [63:0] out_22,
  output [63:0] out_23,
  output [63:0] out_24,
  output [63:0] out_25,
  output [63:0] out_26,
  output [63:0] out_27,
  output [63:0] out_28,
  output [63:0] out_29,
  output [63:0] out_30,
  output [63:0] out_31,
  output [63:0] out_32,
  output [63:0] out_33,
  output [63:0] out_34,
  output [63:0] out_35,
  output [63:0] out_36,
  output [63:0] out_37,
  output [63:0] out_38,
  output [63:0] out_39,
  output [63:0] out_40,
  output [63:0] out_41,
  output [63:0] out_42,
  output [63:0] out_43,
  output [63:0] out_44,
  output [63:0] out_45,
  output [7:0] out_46,
  output [7:0] out_47
);

  wire and_1_out, and_2_out, conditionalinterpreter_1_jump, L0, L1, L2, L3, L4, L5, L6, LI, nor_1_out,
       or_2_out, or_4_out, S0, S1, S2, S3, S4, S5, S6, SO;
  wire [7:0] alu_1_outputdata, ComputerInput, ComputerOutput, ConditionalInstruction,
       conditionalinterpreter_1_jumpaddress, instructiondecoder_1_copy, instructiondecoder_1_immediate,
       instructiondecoder_1_operational, or_3_out, or_5_out, Reg0_t, Reg1_t, Reg2_t, Reg3_t, Reg4_t, Reg5_t,
       Reg6_t;

  and and_1 (and_1_out, instructiondecoder_1_copy[7], ~instructiondecoder_1_copy[6]);  // AND_Gate
  Decoder #(.select(3)) decoder_1 (
    .out0(S0), .out1(S1), .out2(S2), .out3(S3), .out4(S4), .out5(S5), .out6(S6), .out7(SO),
    .sel(instructiondecoder_1_copy[2:0]), .en(and_1_out));
  Decoder #(.select(3)) decoder_2 (
    .out0(L0), .out1(L1), .out2(L2), .out3(L3), .out4(L4), .out5(L5), .out6(L6), .out7(LI),
    .sel(instructiondecoder_1_copy[5:3]), .en(and_1_out));
  ConditionalInterpreter conditionalinterpreter_1 (
    .Reg3(Reg3), .Instruction(ConditionalInstruction), .Reg0(Reg0),
    .JumpAddress(conditionalinterpreter_1_jumpaddress), .Jump(conditionalinterpreter_1_jump));
  assign ComputerOutput = Reg0_t | Reg1_t | Reg2_t | Reg3_t | ComputerInput | Reg6_t | Reg5_t | Reg4_t;  // OR_Gate or_1, 8 bits wide
  Program program_1 (
    .Data(in_3), .Address(in_4), .Clear(in_5), .out_4(out_14), .out_5(out_22), .out_6(out_30),
    .out_7(out_38), .out_8(out_15), .out_9(out_23), .out_10(out_31), .out_11(out_39), .out_12(out_16),
    .out_13(out_24), .out_14(out_32), .out_15(out_40), .out_16(out_17), .out_17(out_25), .out_18(out_33),
    .out_19(out_41), .out_20(out_18), .out_21(out_26), .out_22(out_34), .out_23(out_42), .out_24(out_19),
    .out_25(out_27), .out_26(out_35), .out_27(out_43), .out_28(out_20), .out_29(out_28), .out_30(out_36),
    .out_31(out_44), .out_32(out_21), .out_33(out_29), .out_34(out_37), .out_35(out_45));
  nor nor_1 (nor_1_out, out_46[7], out_46[6]);
  and and_2 (and_2_out, out_46[6], ~out_46[7]);  // AND_Gate
  IP ip_1 (
    .JumpAddress(conditionalinterpreter_1_jumpaddress), .Jump(conditionalinterpreter_1_jump), .Reset(Reset),
    .CurrentAddress(out_47));
  or or_2 (or_2_out, nor_1_out, S0);
  assign or_3_out = instructiondecoder_1_immediate | ComputerOutput;  // OR_Gate or_3, 8 bits wide
  or or_4 (or_4_out, and_2_out, S3);
  assign or_5_out = alu_1_outputdata | ComputerOutput;  // OR_Gate or_5, 8 bits wide
  InstructionDecoder instructiondecoder_1 (
    .in_1(out_46), .Immediate(instructiondecoder_1_immediate),
    .Operational(instructiondecoder_1_operational), .Copy(instructiondecoder_1_copy),
    .Conditional(ConditionalInstruction));
  myRegister myregister_1 (.Load(L0), .Save(or_2_out), .Data(or_3_out), .OutputData(Reg0_t), .AlwaysOutput(Reg0));
  myRegister myregister_2 (.Load(L1), .Save(S1), .Data(ComputerOutput), .OutputData(Reg1_t), .AlwaysOutput(Reg1));
  myRegister myregister_3 (.Load(L2), .Save(S2), .Data(ComputerOutput), .OutputData(Reg2_t), .AlwaysOutput(Reg2));
  myRegister myregister_4 (.Load(L3), .Save(or_4_out), .Data(or_5_out), .OutputData(Reg3_t), .AlwaysOutput(Reg3));
  myRegister myregister_5 (.Load(L4), .Save(S4), .Data(ComputerOutput), .OutputData(Reg4_t), .AlwaysOutput(Reg4));
  myRegister myregister_6 (.Load(L5), .Save(S5), .Data(ComputerOutput), .OutputData(Reg5_t), .AlwaysOutput(Reg5));
  myRegister myregister_7 (.Load(L6), .Save(S6), .Data(ComputerOutput), .OutputData(Reg6_t), .AlwaysOutput(Reg6));
  InstructionReader instructionreader_1 (
    .in_1(out_14), .in_2(out_22), .in_3(out_30), .in_4(out_38), .in_5(out_15), .in_6(out_23), .in_7(out_31),
    .in_8(out_39), .in_9(out_16), .in_10(out_24), .in_11(out_32), .in_12(out_40), .in_13(out_17),
    .in_14(out_25), .in_15(out_33), .in_16(out_41), .in_17(out_18), .in_18(out_26), .in_19(out_34),
    .in_20(out_42), .in_21(out_19), .in_22(out_27), .in_23(out_35), .in_24(out_43), .in_25(out_20),
    .in_26(out_28), .in_27(out_36), .in_28(out_44), .in_29(out_21), .in_30(out_29), .in_31(out_37),
    .in_32(out_45), .Address(out_47), .Instruction(out_46));
  ALU alu_1 (.Instruction(instructiondecoder_1_operational), .A(Reg1), .B(Reg2), .OutputData(alu_1_outputdata));
  Switch8Bit switch8bit_1 (.Enable(LI), .Data(in_2), .OutputData(ComputerInput));
  Switch8Bit switch8bit_2 (.Enable(SO), .Data(ComputerOutput), .OutputData(out_12));

  // Other names for the same wires on the sheet: CurrentReg0[7:0] = Reg0; CurrentReg3[7:0] = Reg3;
  //   Instruction[7:0] = out_46; P0[63:0] = out_14; P1[63:0] = out_22; P2[63:0] = out_30; P3[63:0] = out_38;
  //   P4[63:0] = out_15; P5[63:0] = out_23; P6[63:0] = out_31; P7[63:0] = out_39; P8[63:0] = out_16;
  //   P9[63:0] = out_24; P10[63:0] = out_32; P11[63:0] = out_40; P12[63:0] = out_17; P13[63:0] = out_25;
  //   P14[63:0] = out_33; P15[63:0] = out_41; P16[63:0] = out_18; P17[63:0] = out_26; P18[63:0] = out_34;
  //   P19[63:0] = out_42; P20[63:0] = out_19; P21[63:0] = out_27; P22[63:0] = out_35; P23[63:0] = out_43;
  //   P24[63:0] = out_20; P25[63:0] = out_28; P26[63:0] = out_36; P27[63:0] = out_44; P28[63:0] = out_21;
  //   P29[63:0] = out_29; P30[63:0] = out_37; P31[63:0] = out_45; RIP = Reset
endmodule

module myRegister (
  input  Load,
  input  Save,
  input  [7:0] Data,
  output [7:0] OutputData,
  output [7:0] AlwaysOutput
);

  wire and_1_out, clock_1_out, undriven, undriven_2, undriven_3, undriven_4, undriven_5, undriven_6,
       undriven_7;

  and and_1 (and_1_out, Save, clock_1_out);
  Clock clock_1 (.out(clock_1_out));
  D_Flip_Flop d_ff_1 (.D(Data[0]), .clk(and_1_out), .Q(AlwaysOutput[0]), .reset(undriven));  // open: Qn, preset
  D_Flip_Flop d_ff_2 (
    .D(Data[1]), .clk(and_1_out), .Q(AlwaysOutput[1]), .preset(undriven), .reset(undriven_2));  // open: Qn
  D_Flip_Flop d_ff_3 (
    .D(Data[2]), .clk(and_1_out), .Q(AlwaysOutput[2]), .preset(undriven_2), .reset(undriven_3));  // open: Qn
  D_Flip_Flop d_ff_4 (
    .D(Data[3]), .clk(and_1_out), .Q(AlwaysOutput[3]), .preset(undriven_3), .reset(undriven_4));  // open: Qn
  D_Flip_Flop d_ff_5 (
    .D(Data[4]), .clk(and_1_out), .Q(AlwaysOutput[4]), .preset(undriven_4), .reset(undriven_5));  // open: Qn
  D_Flip_Flop d_ff_6 (
    .D(Data[5]), .clk(and_1_out), .Q(AlwaysOutput[5]), .preset(undriven_5), .reset(undriven_6));  // open: Qn
  D_Flip_Flop d_ff_7 (
    .D(Data[6]), .clk(and_1_out), .Q(AlwaysOutput[6]), .preset(undriven_6), .reset(undriven_7));  // open: Qn
  D_Flip_Flop d_ff_8 (.D(Data[7]), .clk(and_1_out), .Q(AlwaysOutput[7]), .preset(undriven_7));  // open: Qn, reset
  and and_2 (OutputData[0], AlwaysOutput[0], Load);
  and and_3 (OutputData[1], AlwaysOutput[1], Load);
  and and_4 (OutputData[2], AlwaysOutput[2], Load);
  and and_5 (OutputData[3], AlwaysOutput[3], Load);
  and and_6 (OutputData[4], AlwaysOutput[4], Load);
  and and_7 (OutputData[5], AlwaysOutput[5], Load);
  and and_8 (OutputData[6], AlwaysOutput[6], Load);
  and and_9 (OutputData[7], AlwaysOutput[7], Load);
endmodule

module ALU (
  input  [7:0] Instruction,
  input  [7:0] A,
  input  [7:0] B,
  output [7:0] OutputData
);

  wire and_1_out;
  wire [7:0] and_2_out, full8bitadder_1_y, full8bitsubtractor2sc_1_y, nand_1_out, nor_1_out, not_1_out,
       or_1_out;

  assign not_1_out = ~B;  // NOT_Gate not_1, 8 bits wide
  and and_1 (and_1_out, Instruction[6], ~Instruction[7]);  // AND_Gate
  assign or_1_out = A | B;  // OR_Gate or_1, 8 bits wide
  assign nand_1_out = ~(A & B);  // NAND_Gate nand_1, 8 bits wide
  assign nor_1_out = ~(A | B);  // NOR_Gate nor_1, 8 bits wide
  assign and_2_out = A & B;  // AND_Gate and_2, 8 bits wide
  Full8BitAdder full8bitadder_1 (.A(A), .B(B), .Y(full8bitadder_1_y));
  Full8BitSubtractor2sC full8bitsubtractor2sc_1 (.A(A), .B(not_1_out), .Y(full8bitsubtractor2sc_1_y));
  Multiplexer #(.enable("true"), .select(3), .width(8)) multiplexer_1 (
    .in0(or_1_out), .in1(nand_1_out), .in2(nor_1_out), .in3(and_2_out), .in4(full8bitadder_1_y),
    .in5(full8bitsubtractor2sc_1_y), .in6({8{1'b0}}), .in7({8{1'b0}}), .out(OutputData),
    .sel(Instruction[2:0]), .en(and_1_out));
endmodule

module FullAdder (
  input  A,
  input  B,
  input  Cin,
  output S,
  output Cout
);

  wire and_1_out, and_2_out, xor_1_out;

  and and_1 (and_1_out, A, B);
  xor xor_1 (xor_1_out, B, A);
  xor xor_2 (S, Cin, xor_1_out);
  or or_1 (Cout, and_1_out, and_2_out);
  and and_2 (and_2_out, xor_1_out, Cin);
endmodule

module Full8BitAdder (
  input  [7:0] A,
  input  [7:0] B,
  output [7:0] Y
);

  wire fulladder_1_cout, fulladder_2_cout, fulladder_3_cout, fulladder_4_cout, fulladder_5_cout,
       fulladder_6_cout, fulladder_7_cout, fulladder_8_cout;

  FullAdder fulladder_1 (.A(A[0]), .B(B[0]), .Cin(1'b0), .S(Y[0]), .Cout(fulladder_1_cout));
  FullAdder fulladder_2 (.A(A[1]), .B(B[1]), .Cin(fulladder_1_cout), .S(Y[1]), .Cout(fulladder_2_cout));
  FullAdder fulladder_3 (.A(A[2]), .B(B[2]), .Cin(fulladder_2_cout), .S(Y[2]), .Cout(fulladder_3_cout));
  FullAdder fulladder_4 (.A(A[3]), .B(B[3]), .Cin(fulladder_3_cout), .S(Y[3]), .Cout(fulladder_4_cout));
  FullAdder fulladder_5 (.A(A[4]), .B(B[4]), .Cin(fulladder_4_cout), .S(Y[4]), .Cout(fulladder_5_cout));
  FullAdder fulladder_6 (.A(A[5]), .B(B[5]), .Cin(fulladder_5_cout), .S(Y[5]), .Cout(fulladder_6_cout));
  FullAdder fulladder_7 (.A(A[6]), .B(B[6]), .Cin(fulladder_6_cout), .S(Y[6]), .Cout(fulladder_7_cout));
  FullAdder fulladder_8 (.A(A[7]), .B(B[7]), .Cin(fulladder_7_cout), .S(Y[7]), .Cout(fulladder_8_cout));
  // also tied to GND on the sheet: fulladder_8_cout
endmodule

module Full8BitSubtractor2sC (
  input  [7:0] A,
  input  [7:0] B,
  output [7:0] Y
);

  wire fulladder_1_cout, fulladder_2_cout, fulladder_3_cout, fulladder_4_cout, fulladder_5_cout,
       fulladder_6_cout, fulladder_7_cout, fulladder_8_cout;

  FullAdder fulladder_1 (.A(A[0]), .B(B[0]), .Cin(1'b1), .S(Y[0]), .Cout(fulladder_1_cout));
  FullAdder fulladder_2 (.A(A[1]), .B(B[1]), .Cin(fulladder_1_cout), .S(Y[1]), .Cout(fulladder_2_cout));
  FullAdder fulladder_3 (.A(A[2]), .B(B[2]), .Cin(fulladder_2_cout), .S(Y[2]), .Cout(fulladder_3_cout));
  FullAdder fulladder_4 (.A(A[3]), .B(B[3]), .Cin(fulladder_3_cout), .S(Y[3]), .Cout(fulladder_4_cout));
  FullAdder fulladder_5 (.A(A[4]), .B(B[4]), .Cin(fulladder_4_cout), .S(Y[4]), .Cout(fulladder_5_cout));
  FullAdder fulladder_6 (.A(A[5]), .B(B[5]), .Cin(fulladder_5_cout), .S(Y[5]), .Cout(fulladder_6_cout));
  FullAdder fulladder_7 (.A(A[6]), .B(B[6]), .Cin(fulladder_6_cout), .S(Y[6]), .Cout(fulladder_7_cout));
  FullAdder fulladder_8 (.A(A[7]), .B(B[7]), .Cin(fulladder_7_cout), .S(Y[7]), .Cout(fulladder_8_cout));
  // also tied to GND on the sheet: fulladder_8_cout
endmodule

module InstructionDecoder (
  input  [7:0] in_1,
  output [7:0] Immediate,
  output [7:0] Operational,
  output [7:0] Copy,
  output [7:0] Conditional
);

  Demultiplexer #(.select(2), .width(8)) demultiplexer_1 (
    .out0(Immediate), .out1(Operational), .out2(Copy), .out3(Conditional), .in(in_1), .sel(in_1[7:6]));
endmodule

module Sw (
  input  in_1,
  input  [7:0] in_2,
  output [7:0] out_3
);
endmodule

module Program (
  input  [7:0] Data,
  input  [7:0] Address,
  input  Clear,
  output [63:0] out_4,
  output [63:0] out_5,
  output [63:0] out_6,
  output [63:0] out_7,
  output [63:0] out_8,
  output [63:0] out_9,
  output [63:0] out_10,
  output [63:0] out_11,
  output [63:0] out_12,
  output [63:0] out_13,
  output [63:0] out_14,
  output [63:0] out_15,
  output [63:0] out_16,
  output [63:0] out_17,
  output [63:0] out_18,
  output [63:0] out_19,
  output [63:0] out_20,
  output [63:0] out_21,
  output [63:0] out_22,
  output [63:0] out_23,
  output [63:0] out_24,
  output [63:0] out_25,
  output [63:0] out_26,
  output [63:0] out_27,
  output [63:0] out_28,
  output [63:0] out_29,
  output [63:0] out_30,
  output [63:0] out_31,
  output [63:0] out_32,
  output [63:0] out_33,
  output [63:0] out_34,
  output [63:0] out_35
);

  MemoryChip128B memorychip128b_1 (
    .Data(Data), .Address(Address), .Clear(Clear), .Bit7(1'b0), .Y0_7(out_4), .Y8_15(out_5), .Y16_23(out_6),
    .Y24_31(out_7), .Y32_39(out_8), .Y40_47(out_9), .Y48_55(out_10), .Y56_63(out_11), .Y64_71(out_12),
    .Y72_79(out_13), .Y80_87(out_14), .Y88_95(out_15), .Y96_103(out_16), .Y104_111(out_17),
    .Y112_119(out_18), .Y120_127(out_19));
  MemoryChip128B memorychip128b_2 (
    .Data(Data), .Address(Address), .Clear(Clear), .Bit7(1'b1), .Y0_7(out_20), .Y8_15(out_21),
    .Y16_23(out_22), .Y24_31(out_23), .Y32_39(out_24), .Y40_47(out_25), .Y48_55(out_26), .Y56_63(out_27),
    .Y64_71(out_28), .Y72_79(out_29), .Y80_87(out_30), .Y88_95(out_31), .Y96_103(out_32), .Y104_111(out_33),
    .Y112_119(out_34), .Y120_127(out_35));
endmodule

module ByteCell (
  input  [7:0] data,
  input  write,
  input  clear,
  output [7:0] out_4
);

  wire and_1_out, clock_1_out;

  and and_1 (and_1_out, write, clock_1_out);
  Clock clock_1 (.out(clock_1_out));
  D_Flip_Flop d_ff_1 (.D(data[0]), .clk(and_1_out), .Q(out_4[0]), .reset(clear));  // open: Qn, preset
  D_Flip_Flop d_ff_2 (.D(data[1]), .clk(and_1_out), .Q(out_4[1]), .reset(clear));  // open: Qn, preset
  D_Flip_Flop d_ff_3 (.D(data[2]), .clk(and_1_out), .Q(out_4[2]), .reset(clear));  // open: Qn, preset
  D_Flip_Flop d_ff_4 (.D(data[3]), .clk(and_1_out), .Q(out_4[3]), .reset(clear));  // open: Qn, preset
  D_Flip_Flop d_ff_5 (.D(data[4]), .clk(and_1_out), .Q(out_4[4]), .reset(clear));  // open: Qn, preset
  D_Flip_Flop d_ff_6 (.D(data[5]), .clk(and_1_out), .Q(out_4[5]), .reset(clear));  // open: Qn, preset
  D_Flip_Flop d_ff_7 (.D(data[6]), .clk(and_1_out), .Q(out_4[6]), .reset(clear));  // open: Qn, preset
  D_Flip_Flop d_ff_8 (.D(data[7]), .clk(and_1_out), .Q(out_4[7]), .reset(clear));  // open: Qn, preset
endmodule

module MemoryChip128B (
  input  [7:0] Data,
  input  [7:0] Address,
  input  Clear,
  input  Bit7,
  output [63:0] Y0_7,
  output [63:0] Y8_15,
  output [63:0] Y16_23,
  output [63:0] Y24_31,
  output [63:0] Y32_39,
  output [63:0] Y40_47,
  output [63:0] Y48_55,
  output [63:0] Y56_63,
  output [63:0] Y64_71,
  output [63:0] Y72_79,
  output [63:0] Y80_87,
  output [63:0] Y88_95,
  output [63:0] Y96_103,
  output [63:0] Y104_111,
  output [63:0] Y112_119,
  output [63:0] Y120_127
);

  wire and_1_out, decoder_1_out0, decoder_1_out1, decoder_1_out2, decoder_1_out3, decoder_1_out4,
       decoder_1_out5, decoder_1_out6, decoder_1_out7, decoder_2_out0, decoder_2_out1, decoder_2_out2,
       decoder_2_out3, decoder_2_out4, decoder_2_out5, decoder_2_out6, decoder_2_out7, decoder_3_out0,
       decoder_3_out1, decoder_3_out2, decoder_3_out3, decoder_3_out4, decoder_3_out5, decoder_3_out6,
       decoder_3_out7, decoder_4_out0, decoder_4_out1, decoder_4_out2, decoder_4_out3, decoder_4_out4,
       decoder_4_out5, decoder_4_out6, decoder_4_out7, decoder_5_out0, decoder_5_out1, decoder_5_out2,
       decoder_5_out3, decoder_5_out4, decoder_5_out5, decoder_5_out6, decoder_5_out7, decoder_6_out0,
       decoder_6_out1, decoder_6_out2, decoder_6_out3, decoder_6_out4, decoder_6_out5, decoder_6_out6,
       decoder_6_out7, decoder_7_out0, decoder_7_out1, decoder_7_out2, decoder_7_out3, decoder_7_out4,
       decoder_7_out5, decoder_7_out6, decoder_7_out7, decoder_8_out0, decoder_8_out1, decoder_8_out2,
       decoder_8_out3, decoder_8_out4, decoder_8_out5, decoder_8_out6, decoder_8_out7, decoder_9_out0,
       decoder_9_out1, decoder_9_out2, decoder_9_out3, decoder_9_out4, decoder_9_out5, decoder_9_out6,
       decoder_9_out7, decoder_10_out0, decoder_10_out1, decoder_10_out2, decoder_10_out3, decoder_10_out4,
       decoder_10_out5, decoder_10_out6, decoder_10_out7, decoder_11_out0, decoder_11_out1, decoder_11_out2,
       decoder_11_out3, decoder_11_out4, decoder_11_out5, decoder_11_out6, decoder_11_out7, decoder_12_out0,
       decoder_12_out1, decoder_12_out2, decoder_12_out3, decoder_12_out4, decoder_12_out5, decoder_12_out6,
       decoder_12_out7, decoder_13_out0, decoder_13_out1, decoder_13_out2, decoder_13_out3, decoder_13_out4,
       decoder_13_out5, decoder_13_out6, decoder_13_out7, decoder_14_out0, decoder_14_out1, decoder_14_out2,
       decoder_14_out3, decoder_14_out4, decoder_14_out5, decoder_14_out6, decoder_14_out7, decoder_15_out0,
       decoder_15_out1, decoder_15_out2, decoder_15_out3, decoder_15_out4, decoder_15_out5, decoder_15_out6,
       decoder_15_out7, decoder_16_out0, decoder_16_out1, decoder_16_out2, decoder_16_out3, decoder_16_out4,
       decoder_16_out5, decoder_16_out6, decoder_16_out7, decoder_17_out0, decoder_17_out1, decoder_17_out2,
       decoder_17_out3, decoder_17_out4, decoder_17_out5, decoder_17_out6, decoder_17_out7, decoder_18_out0,
       decoder_18_out1, decoder_18_out2, decoder_18_out3, decoder_18_out4, decoder_18_out5, decoder_18_out6,
       decoder_18_out7, nor_1_out, xor_1_out, xor_2_out;
  wire [2:0] demultiplexer_1_out0, demultiplexer_1_out1, demultiplexer_2_out0, demultiplexer_2_out1,
       demultiplexer_2_out2, demultiplexer_2_out3, demultiplexer_2_out4, demultiplexer_2_out5,
       demultiplexer_2_out6, demultiplexer_2_out7, demultiplexer_3_out0, demultiplexer_3_out1,
       demultiplexer_3_out2, demultiplexer_3_out3, demultiplexer_3_out4, demultiplexer_3_out5,
       demultiplexer_3_out6, demultiplexer_3_out7;

  Demultiplexer #(.tristate("true"), .width(3)) demultiplexer_1 (
    .out0(demultiplexer_1_out0), .out1(demultiplexer_1_out1), .in(Address[2:0]), .sel(Address[6]));
  xor xor_1 (xor_1_out, Bit7, Address[7]);
  nor nor_1 (nor_1_out, xor_1_out, Address[6]);
  Decoder #(.select(3)) decoder_1 (
    .out0(decoder_1_out0), .out1(decoder_1_out1), .out2(decoder_1_out2), .out3(decoder_1_out3),
    .out4(decoder_1_out4), .out5(decoder_1_out5), .out6(decoder_1_out6), .out7(decoder_1_out7),
    .sel(Address[5:3]), .en(nor_1_out));
  Demultiplexer #(.select(3), .width(3)) demultiplexer_2 (
    .out0(demultiplexer_2_out0), .out1(demultiplexer_2_out1), .out2(demultiplexer_2_out2),
    .out3(demultiplexer_2_out3), .out4(demultiplexer_2_out4), .out5(demultiplexer_2_out5),
    .out6(demultiplexer_2_out6), .out7(demultiplexer_2_out7), .in(demultiplexer_1_out0), .sel(Address[5:3]));
  Decoder #(.select(3)) decoder_2 (
    .out0(decoder_2_out0), .out1(decoder_2_out1), .out2(decoder_2_out2), .out3(decoder_2_out3),
    .out4(decoder_2_out4), .out5(decoder_2_out5), .out6(decoder_2_out6), .out7(decoder_2_out7),
    .sel(Address[5:3]), .en(and_1_out));
  xor xor_2 (xor_2_out, Bit7, Address[7]);
  and and_1 (and_1_out, ~xor_2_out, Address[6]);  // AND_Gate
  Demultiplexer #(.select(3), .width(3)) demultiplexer_3 (
    .out0(demultiplexer_3_out0), .out1(demultiplexer_3_out1), .out2(demultiplexer_3_out2),
    .out3(demultiplexer_3_out3), .out4(demultiplexer_3_out4), .out5(demultiplexer_3_out5),
    .out6(demultiplexer_3_out6), .out7(demultiplexer_3_out7), .in(demultiplexer_1_out1), .sel(Address[5:3]));
  Decoder #(.select(3)) decoder_3 (
    .out0(decoder_3_out0), .out1(decoder_3_out1), .out2(decoder_3_out2), .out3(decoder_3_out3),
    .out4(decoder_3_out4), .out5(decoder_3_out5), .out6(decoder_3_out6), .out7(decoder_3_out7),
    .sel(demultiplexer_2_out0), .en(decoder_1_out0));
  Decoder #(.select(3)) decoder_4 (
    .out0(decoder_4_out0), .out1(decoder_4_out1), .out2(decoder_4_out2), .out3(decoder_4_out3),
    .out4(decoder_4_out4), .out5(decoder_4_out5), .out6(decoder_4_out6), .out7(decoder_4_out7),
    .sel(demultiplexer_3_out0), .en(decoder_2_out0));
  ByteCell bytecell_1 (.data(Data), .write(decoder_3_out0), .clear(Clear), .out_4(Y0_7[63:56]));
  ByteCell bytecell_2 (.data(Data), .write(decoder_3_out1), .clear(Clear), .out_4(Y0_7[55:48]));
  ByteCell bytecell_3 (.data(Data), .write(decoder_3_out2), .clear(Clear), .out_4(Y0_7[47:40]));
  ByteCell bytecell_4 (.data(Data), .write(decoder_3_out3), .clear(Clear), .out_4(Y0_7[39:32]));
  ByteCell bytecell_5 (.data(Data), .write(decoder_3_out4), .clear(Clear), .out_4(Y0_7[31:24]));
  ByteCell bytecell_6 (.data(Data), .write(decoder_3_out5), .clear(Clear), .out_4(Y0_7[23:16]));
  ByteCell bytecell_7 (.data(Data), .write(decoder_3_out6), .clear(Clear), .out_4(Y0_7[15:8]));
  ByteCell bytecell_8 (.data(Data), .write(decoder_3_out7), .clear(Clear), .out_4(Y0_7[7:0]));
  ByteCell bytecell_9 (.data(Data), .write(decoder_4_out0), .clear(Clear), .out_4(Y64_71[63:56]));
  ByteCell bytecell_10 (.data(Data), .write(decoder_4_out1), .clear(Clear), .out_4(Y64_71[55:48]));
  ByteCell bytecell_11 (.data(Data), .write(decoder_4_out2), .clear(Clear), .out_4(Y64_71[47:40]));
  ByteCell bytecell_12 (.data(Data), .write(decoder_4_out3), .clear(Clear), .out_4(Y64_71[39:32]));
  ByteCell bytecell_13 (.data(Data), .write(decoder_4_out4), .clear(Clear), .out_4(Y64_71[31:24]));
  ByteCell bytecell_14 (.data(Data), .write(decoder_4_out5), .clear(Clear), .out_4(Y64_71[23:16]));
  ByteCell bytecell_15 (.data(Data), .write(decoder_4_out6), .clear(Clear), .out_4(Y64_71[15:8]));
  ByteCell bytecell_16 (.data(Data), .write(decoder_4_out7), .clear(Clear), .out_4(Y64_71[7:0]));
  Decoder #(.select(3)) decoder_5 (
    .out0(decoder_5_out0), .out1(decoder_5_out1), .out2(decoder_5_out2), .out3(decoder_5_out3),
    .out4(decoder_5_out4), .out5(decoder_5_out5), .out6(decoder_5_out6), .out7(decoder_5_out7),
    .sel(demultiplexer_2_out1), .en(decoder_1_out1));
  Decoder #(.select(3)) decoder_6 (
    .out0(decoder_6_out0), .out1(decoder_6_out1), .out2(decoder_6_out2), .out3(decoder_6_out3),
    .out4(decoder_6_out4), .out5(decoder_6_out5), .out6(decoder_6_out6), .out7(decoder_6_out7),
    .sel(demultiplexer_3_out1), .en(decoder_2_out1));
  ByteCell bytecell_17 (.data(Data), .write(decoder_5_out0), .clear(Clear), .out_4(Y8_15[63:56]));
  ByteCell bytecell_18 (.data(Data), .write(decoder_5_out1), .clear(Clear), .out_4(Y8_15[55:48]));
  ByteCell bytecell_19 (.data(Data), .write(decoder_5_out2), .clear(Clear), .out_4(Y8_15[47:40]));
  ByteCell bytecell_20 (.data(Data), .write(decoder_5_out3), .clear(Clear), .out_4(Y8_15[39:32]));
  ByteCell bytecell_21 (.data(Data), .write(decoder_5_out4), .clear(Clear), .out_4(Y8_15[31:24]));
  ByteCell bytecell_22 (.data(Data), .write(decoder_5_out5), .clear(Clear), .out_4(Y8_15[23:16]));
  ByteCell bytecell_23 (.data(Data), .write(decoder_5_out6), .clear(Clear), .out_4(Y8_15[15:8]));
  ByteCell bytecell_24 (.data(Data), .write(decoder_5_out7), .clear(Clear), .out_4(Y8_15[7:0]));
  ByteCell bytecell_25 (.data(Data), .write(decoder_6_out0), .clear(Clear), .out_4(Y72_79[63:56]));
  ByteCell bytecell_26 (.data(Data), .write(decoder_6_out1), .clear(Clear), .out_4(Y72_79[55:48]));
  ByteCell bytecell_27 (.data(Data), .write(decoder_6_out2), .clear(Clear), .out_4(Y72_79[47:40]));
  ByteCell bytecell_28 (.data(Data), .write(decoder_6_out3), .clear(Clear), .out_4(Y72_79[39:32]));
  ByteCell bytecell_29 (.data(Data), .write(decoder_6_out4), .clear(Clear), .out_4(Y72_79[31:24]));
  ByteCell bytecell_30 (.data(Data), .write(decoder_6_out5), .clear(Clear), .out_4(Y72_79[23:16]));
  ByteCell bytecell_31 (.data(Data), .write(decoder_6_out6), .clear(Clear), .out_4(Y72_79[15:8]));
  ByteCell bytecell_32 (.data(Data), .write(decoder_6_out7), .clear(Clear), .out_4(Y72_79[7:0]));
  Decoder #(.select(3)) decoder_7 (
    .out0(decoder_7_out0), .out1(decoder_7_out1), .out2(decoder_7_out2), .out3(decoder_7_out3),
    .out4(decoder_7_out4), .out5(decoder_7_out5), .out6(decoder_7_out6), .out7(decoder_7_out7),
    .sel(demultiplexer_2_out2), .en(decoder_1_out2));
  Decoder #(.select(3)) decoder_8 (
    .out0(decoder_8_out0), .out1(decoder_8_out1), .out2(decoder_8_out2), .out3(decoder_8_out3),
    .out4(decoder_8_out4), .out5(decoder_8_out5), .out6(decoder_8_out6), .out7(decoder_8_out7),
    .sel(demultiplexer_3_out2), .en(decoder_2_out2));
  ByteCell bytecell_33 (.data(Data), .write(decoder_7_out0), .clear(Clear), .out_4(Y16_23[63:56]));
  ByteCell bytecell_34 (.data(Data), .write(decoder_7_out1), .clear(Clear), .out_4(Y16_23[55:48]));
  ByteCell bytecell_35 (.data(Data), .write(decoder_7_out2), .clear(Clear), .out_4(Y16_23[47:40]));
  ByteCell bytecell_36 (.data(Data), .write(decoder_7_out3), .clear(Clear), .out_4(Y16_23[39:32]));
  ByteCell bytecell_37 (.data(Data), .write(decoder_7_out4), .clear(Clear), .out_4(Y16_23[31:24]));
  ByteCell bytecell_38 (.data(Data), .write(decoder_7_out5), .clear(Clear), .out_4(Y16_23[23:16]));
  ByteCell bytecell_39 (.data(Data), .write(decoder_7_out6), .clear(Clear), .out_4(Y16_23[15:8]));
  ByteCell bytecell_40 (.data(Data), .write(decoder_7_out7), .clear(Clear), .out_4(Y16_23[7:0]));
  ByteCell bytecell_41 (.data(Data), .write(decoder_8_out0), .clear(Clear), .out_4(Y80_87[63:56]));
  ByteCell bytecell_42 (.data(Data), .write(decoder_8_out1), .clear(Clear), .out_4(Y80_87[55:48]));
  ByteCell bytecell_43 (.data(Data), .write(decoder_8_out2), .clear(Clear), .out_4(Y80_87[47:40]));
  ByteCell bytecell_44 (.data(Data), .write(decoder_8_out3), .clear(Clear), .out_4(Y80_87[39:32]));
  ByteCell bytecell_45 (.data(Data), .write(decoder_8_out4), .clear(Clear), .out_4(Y80_87[31:24]));
  ByteCell bytecell_46 (.data(Data), .write(decoder_8_out5), .clear(Clear), .out_4(Y80_87[23:16]));
  ByteCell bytecell_47 (.data(Data), .write(decoder_8_out6), .clear(Clear), .out_4(Y80_87[15:8]));
  ByteCell bytecell_48 (.data(Data), .write(decoder_8_out7), .clear(Clear), .out_4(Y80_87[7:0]));
  Decoder #(.select(3)) decoder_9 (
    .out0(decoder_9_out0), .out1(decoder_9_out1), .out2(decoder_9_out2), .out3(decoder_9_out3),
    .out4(decoder_9_out4), .out5(decoder_9_out5), .out6(decoder_9_out6), .out7(decoder_9_out7),
    .sel(demultiplexer_2_out3), .en(decoder_1_out3));
  Decoder #(.select(3)) decoder_10 (
    .out0(decoder_10_out0), .out1(decoder_10_out1), .out2(decoder_10_out2), .out3(decoder_10_out3),
    .out4(decoder_10_out4), .out5(decoder_10_out5), .out6(decoder_10_out6), .out7(decoder_10_out7),
    .sel(demultiplexer_3_out3), .en(decoder_2_out3));
  ByteCell bytecell_49 (.data(Data), .write(decoder_9_out0), .clear(Clear), .out_4(Y24_31[63:56]));
  ByteCell bytecell_50 (.data(Data), .write(decoder_9_out1), .clear(Clear), .out_4(Y24_31[55:48]));
  ByteCell bytecell_51 (.data(Data), .write(decoder_9_out2), .clear(Clear), .out_4(Y24_31[47:40]));
  ByteCell bytecell_52 (.data(Data), .write(decoder_9_out3), .clear(Clear), .out_4(Y24_31[39:32]));
  ByteCell bytecell_53 (.data(Data), .write(decoder_9_out4), .clear(Clear), .out_4(Y24_31[31:24]));
  ByteCell bytecell_54 (.data(Data), .write(decoder_9_out5), .clear(Clear), .out_4(Y24_31[23:16]));
  ByteCell bytecell_55 (.data(Data), .write(decoder_9_out6), .clear(Clear), .out_4(Y24_31[15:8]));
  ByteCell bytecell_56 (.data(Data), .write(decoder_9_out7), .clear(Clear), .out_4(Y24_31[7:0]));
  ByteCell bytecell_57 (.data(Data), .write(decoder_10_out0), .clear(Clear), .out_4(Y88_95[63:56]));
  ByteCell bytecell_58 (.data(Data), .write(decoder_10_out1), .clear(Clear), .out_4(Y88_95[55:48]));
  ByteCell bytecell_59 (.data(Data), .write(decoder_10_out2), .clear(Clear), .out_4(Y88_95[47:40]));
  ByteCell bytecell_60 (.data(Data), .write(decoder_10_out3), .clear(Clear), .out_4(Y88_95[39:32]));
  ByteCell bytecell_61 (.data(Data), .write(decoder_10_out4), .clear(Clear), .out_4(Y88_95[31:24]));
  ByteCell bytecell_62 (.data(Data), .write(decoder_10_out5), .clear(Clear), .out_4(Y88_95[23:16]));
  ByteCell bytecell_63 (.data(Data), .write(decoder_10_out6), .clear(Clear), .out_4(Y88_95[15:8]));
  ByteCell bytecell_64 (.data(Data), .write(decoder_10_out7), .clear(Clear), .out_4(Y88_95[7:0]));
  Decoder #(.select(3)) decoder_11 (
    .out0(decoder_11_out0), .out1(decoder_11_out1), .out2(decoder_11_out2), .out3(decoder_11_out3),
    .out4(decoder_11_out4), .out5(decoder_11_out5), .out6(decoder_11_out6), .out7(decoder_11_out7),
    .sel(demultiplexer_2_out4), .en(decoder_1_out4));
  Decoder #(.select(3)) decoder_12 (
    .out0(decoder_12_out0), .out1(decoder_12_out1), .out2(decoder_12_out2), .out3(decoder_12_out3),
    .out4(decoder_12_out4), .out5(decoder_12_out5), .out6(decoder_12_out6), .out7(decoder_12_out7),
    .sel(demultiplexer_3_out4), .en(decoder_2_out4));
  ByteCell bytecell_65 (.data(Data), .write(decoder_11_out0), .clear(Clear), .out_4(Y32_39[63:56]));
  ByteCell bytecell_66 (.data(Data), .write(decoder_11_out1), .clear(Clear), .out_4(Y32_39[55:48]));
  ByteCell bytecell_67 (.data(Data), .write(decoder_11_out2), .clear(Clear), .out_4(Y32_39[47:40]));
  ByteCell bytecell_68 (.data(Data), .write(decoder_11_out3), .clear(Clear), .out_4(Y32_39[39:32]));
  ByteCell bytecell_69 (.data(Data), .write(decoder_11_out4), .clear(Clear), .out_4(Y32_39[31:24]));
  ByteCell bytecell_70 (.data(Data), .write(decoder_11_out5), .clear(Clear), .out_4(Y32_39[23:16]));
  ByteCell bytecell_71 (.data(Data), .write(decoder_11_out6), .clear(Clear), .out_4(Y32_39[15:8]));
  ByteCell bytecell_72 (.data(Data), .write(decoder_11_out7), .clear(Clear), .out_4(Y32_39[7:0]));
  ByteCell bytecell_73 (.data(Data), .write(decoder_12_out0), .clear(Clear), .out_4(Y96_103[63:56]));
  ByteCell bytecell_74 (.data(Data), .write(decoder_12_out1), .clear(Clear), .out_4(Y96_103[55:48]));
  ByteCell bytecell_75 (.data(Data), .write(decoder_12_out2), .clear(Clear), .out_4(Y96_103[47:40]));
  ByteCell bytecell_76 (.data(Data), .write(decoder_12_out3), .clear(Clear), .out_4(Y96_103[39:32]));
  ByteCell bytecell_77 (.data(Data), .write(decoder_12_out4), .clear(Clear), .out_4(Y96_103[31:24]));
  ByteCell bytecell_78 (.data(Data), .write(decoder_12_out5), .clear(Clear), .out_4(Y96_103[23:16]));
  ByteCell bytecell_79 (.data(Data), .write(decoder_12_out6), .clear(Clear), .out_4(Y96_103[15:8]));
  ByteCell bytecell_80 (.data(Data), .write(decoder_12_out7), .clear(Clear), .out_4(Y96_103[7:0]));
  Decoder #(.select(3)) decoder_13 (
    .out0(decoder_13_out0), .out1(decoder_13_out1), .out2(decoder_13_out2), .out3(decoder_13_out3),
    .out4(decoder_13_out4), .out5(decoder_13_out5), .out6(decoder_13_out6), .out7(decoder_13_out7),
    .sel(demultiplexer_2_out5), .en(decoder_1_out5));
  Decoder #(.select(3)) decoder_14 (
    .out0(decoder_14_out0), .out1(decoder_14_out1), .out2(decoder_14_out2), .out3(decoder_14_out3),
    .out4(decoder_14_out4), .out5(decoder_14_out5), .out6(decoder_14_out6), .out7(decoder_14_out7),
    .sel(demultiplexer_3_out5), .en(decoder_2_out5));
  ByteCell bytecell_81 (.data(Data), .write(decoder_13_out0), .clear(Clear), .out_4(Y40_47[63:56]));
  ByteCell bytecell_82 (.data(Data), .write(decoder_13_out1), .clear(Clear), .out_4(Y40_47[55:48]));
  ByteCell bytecell_83 (.data(Data), .write(decoder_13_out2), .clear(Clear), .out_4(Y40_47[47:40]));
  ByteCell bytecell_84 (.data(Data), .write(decoder_13_out3), .clear(Clear), .out_4(Y40_47[39:32]));
  ByteCell bytecell_85 (.data(Data), .write(decoder_13_out4), .clear(Clear), .out_4(Y40_47[31:24]));
  ByteCell bytecell_86 (.data(Data), .write(decoder_13_out5), .clear(Clear), .out_4(Y40_47[23:16]));
  ByteCell bytecell_87 (.data(Data), .write(decoder_13_out6), .clear(Clear), .out_4(Y40_47[15:8]));
  ByteCell bytecell_88 (.data(Data), .write(decoder_13_out7), .clear(Clear), .out_4(Y40_47[7:0]));
  ByteCell bytecell_89 (.data(Data), .write(decoder_14_out0), .clear(Clear), .out_4(Y104_111[63:56]));
  ByteCell bytecell_90 (.data(Data), .write(decoder_14_out1), .clear(Clear), .out_4(Y104_111[55:48]));
  ByteCell bytecell_91 (.data(Data), .write(decoder_14_out2), .clear(Clear), .out_4(Y104_111[47:40]));
  ByteCell bytecell_92 (.data(Data), .write(decoder_14_out3), .clear(Clear), .out_4(Y104_111[39:32]));
  ByteCell bytecell_93 (.data(Data), .write(decoder_14_out4), .clear(Clear), .out_4(Y104_111[31:24]));
  ByteCell bytecell_94 (.data(Data), .write(decoder_14_out5), .clear(Clear), .out_4(Y104_111[23:16]));
  ByteCell bytecell_95 (.data(Data), .write(decoder_14_out6), .clear(Clear), .out_4(Y104_111[15:8]));
  ByteCell bytecell_96 (.data(Data), .write(decoder_14_out7), .clear(Clear), .out_4(Y104_111[7:0]));
  Decoder #(.select(3)) decoder_15 (
    .out0(decoder_15_out0), .out1(decoder_15_out1), .out2(decoder_15_out2), .out3(decoder_15_out3),
    .out4(decoder_15_out4), .out5(decoder_15_out5), .out6(decoder_15_out6), .out7(decoder_15_out7),
    .sel(demultiplexer_2_out6), .en(decoder_1_out6));
  Decoder #(.select(3)) decoder_16 (
    .out0(decoder_16_out0), .out1(decoder_16_out1), .out2(decoder_16_out2), .out3(decoder_16_out3),
    .out4(decoder_16_out4), .out5(decoder_16_out5), .out6(decoder_16_out6), .out7(decoder_16_out7),
    .sel(demultiplexer_3_out6), .en(decoder_2_out6));
  ByteCell bytecell_97 (.data(Data), .write(decoder_15_out0), .clear(Clear), .out_4(Y48_55[63:56]));
  ByteCell bytecell_98 (.data(Data), .write(decoder_15_out1), .clear(Clear), .out_4(Y48_55[55:48]));
  ByteCell bytecell_99 (.data(Data), .write(decoder_15_out2), .clear(Clear), .out_4(Y48_55[47:40]));
  ByteCell bytecell_100 (.data(Data), .write(decoder_15_out3), .clear(Clear), .out_4(Y48_55[39:32]));
  ByteCell bytecell_101 (.data(Data), .write(decoder_15_out4), .clear(Clear), .out_4(Y48_55[31:24]));
  ByteCell bytecell_102 (.data(Data), .write(decoder_15_out5), .clear(Clear), .out_4(Y48_55[23:16]));
  ByteCell bytecell_103 (.data(Data), .write(decoder_15_out6), .clear(Clear), .out_4(Y48_55[15:8]));
  ByteCell bytecell_104 (.data(Data), .write(decoder_15_out7), .clear(Clear), .out_4(Y48_55[7:0]));
  ByteCell bytecell_105 (.data(Data), .write(decoder_16_out0), .clear(Clear), .out_4(Y112_119[63:56]));
  ByteCell bytecell_106 (.data(Data), .write(decoder_16_out1), .clear(Clear), .out_4(Y112_119[55:48]));
  ByteCell bytecell_107 (.data(Data), .write(decoder_16_out2), .clear(Clear), .out_4(Y112_119[47:40]));
  ByteCell bytecell_108 (.data(Data), .write(decoder_16_out3), .clear(Clear), .out_4(Y112_119[39:32]));
  ByteCell bytecell_109 (.data(Data), .write(decoder_16_out4), .clear(Clear), .out_4(Y112_119[31:24]));
  ByteCell bytecell_110 (.data(Data), .write(decoder_16_out5), .clear(Clear), .out_4(Y112_119[23:16]));
  ByteCell bytecell_111 (.data(Data), .write(decoder_16_out6), .clear(Clear), .out_4(Y112_119[15:8]));
  ByteCell bytecell_112 (.data(Data), .write(decoder_16_out7), .clear(Clear), .out_4(Y112_119[7:0]));
  Decoder #(.select(3)) decoder_17 (
    .out0(decoder_17_out0), .out1(decoder_17_out1), .out2(decoder_17_out2), .out3(decoder_17_out3),
    .out4(decoder_17_out4), .out5(decoder_17_out5), .out6(decoder_17_out6), .out7(decoder_17_out7),
    .sel(demultiplexer_2_out7), .en(decoder_1_out7));
  Decoder #(.select(3)) decoder_18 (
    .out0(decoder_18_out0), .out1(decoder_18_out1), .out2(decoder_18_out2), .out3(decoder_18_out3),
    .out4(decoder_18_out4), .out5(decoder_18_out5), .out6(decoder_18_out6), .out7(decoder_18_out7),
    .sel(demultiplexer_3_out7), .en(decoder_2_out7));
  ByteCell bytecell_113 (.data(Data), .write(decoder_17_out0), .clear(Clear), .out_4(Y56_63[63:56]));
  ByteCell bytecell_114 (.data(Data), .write(decoder_17_out1), .clear(Clear), .out_4(Y56_63[55:48]));
  ByteCell bytecell_115 (.data(Data), .write(decoder_17_out2), .clear(Clear), .out_4(Y56_63[47:40]));
  ByteCell bytecell_116 (.data(Data), .write(decoder_17_out3), .clear(Clear), .out_4(Y56_63[39:32]));
  ByteCell bytecell_117 (.data(Data), .write(decoder_17_out4), .clear(Clear), .out_4(Y56_63[31:24]));
  ByteCell bytecell_118 (.data(Data), .write(decoder_17_out5), .clear(Clear), .out_4(Y56_63[23:16]));
  ByteCell bytecell_119 (.data(Data), .write(decoder_17_out6), .clear(Clear), .out_4(Y56_63[15:8]));
  ByteCell bytecell_120 (.data(Data), .write(decoder_17_out7), .clear(Clear), .out_4(Y56_63[7:0]));
  ByteCell bytecell_121 (.data(Data), .write(decoder_18_out0), .clear(Clear), .out_4(Y120_127[63:56]));
  ByteCell bytecell_122 (.data(Data), .write(decoder_18_out1), .clear(Clear), .out_4(Y120_127[55:48]));
  ByteCell bytecell_123 (.data(Data), .write(decoder_18_out2), .clear(Clear), .out_4(Y120_127[47:40]));
  ByteCell bytecell_124 (.data(Data), .write(decoder_18_out3), .clear(Clear), .out_4(Y120_127[39:32]));
  ByteCell bytecell_125 (.data(Data), .write(decoder_18_out4), .clear(Clear), .out_4(Y120_127[31:24]));
  ByteCell bytecell_126 (.data(Data), .write(decoder_18_out5), .clear(Clear), .out_4(Y120_127[23:16]));
  ByteCell bytecell_127 (.data(Data), .write(decoder_18_out6), .clear(Clear), .out_4(Y120_127[15:8]));
  ByteCell bytecell_128 (.data(Data), .write(decoder_18_out7), .clear(Clear), .out_4(Y120_127[7:0]));
endmodule

module InstructionReader (
  input  [63:0] in_1,
  input  [63:0] in_2,
  input  [63:0] in_3,
  input  [63:0] in_4,
  input  [63:0] in_5,
  input  [63:0] in_6,
  input  [63:0] in_7,
  input  [63:0] in_8,
  input  [63:0] in_9,
  input  [63:0] in_10,
  input  [63:0] in_11,
  input  [63:0] in_12,
  input  [63:0] in_13,
  input  [63:0] in_14,
  input  [63:0] in_15,
  input  [63:0] in_16,
  input  [63:0] in_17,
  input  [63:0] in_18,
  input  [63:0] in_19,
  input  [63:0] in_20,
  input  [63:0] in_21,
  input  [63:0] in_22,
  input  [63:0] in_23,
  input  [63:0] in_24,
  input  [63:0] in_25,
  input  [63:0] in_26,
  input  [63:0] in_27,
  input  [63:0] in_28,
  input  [63:0] in_29,
  input  [63:0] in_30,
  input  [63:0] in_31,
  input  [63:0] in_32,
  input  [7:0] Address,
  output [7:0] Instruction
);

  wire [63:0] multiplexer_1_out;

  Multiplexer #(.select(5), .width(64)) multiplexer_1 (
    .in0(in_1), .in1(in_2), .in2(in_3), .in3(in_4), .in4(in_5), .in5(in_6), .in6(in_7), .in7(in_8),
    .in8(in_9), .in9(in_10), .in10(in_11), .in11(in_12), .in12(in_13), .in13(in_14), .in14(in_15),
    .in15(in_16), .in16(in_17), .in17(in_18), .in18(in_19), .in19(in_20), .in20(in_21), .in21(in_22),
    .in22(in_23), .in23(in_24), .in24(in_25), .in25(in_26), .in26(in_27), .in27(in_28), .in28(in_29),
    .in29(in_30), .in30(in_31), .in31(in_32), .out(multiplexer_1_out), .sel(Address[7:3]));
  Multiplexer #(.select(3), .width(8)) multiplexer_2 (
    .in0(multiplexer_1_out[63:56]), .in1(multiplexer_1_out[55:48]), .in2(multiplexer_1_out[47:40]),
    .in3(multiplexer_1_out[39:32]), .in4(multiplexer_1_out[31:24]), .in5(multiplexer_1_out[23:16]),
    .in6(multiplexer_1_out[15:8]), .in7(multiplexer_1_out[7:0]), .out(Instruction), .sel(Address[2:0]));
endmodule

module IP (
  input  [7:0] JumpAddress,
  input  Jump,
  input  Reset,
  output [7:0] CurrentAddress
);

  wire and_1_out, and_2_out, and_3_out, and_4_out, and_5_out, and_6_out, and_7_out, and_8_out, and_9_out,
       and_10_out, and_11_out, and_12_out, and_13_out, and_14_out, and_15_out, and_16_out, and_17_out,
       and_18_out, and_19_out, and_20_out, and_21_out, and_22_out, clock_1_out, not_1_out, not_2_out,
       not_3_out, not_4_out, not_5_out, not_6_out, not_7_out, not_8_out, or_1_out, or_2_out, or_3_out,
       or_4_out, or_5_out, or_6_out, or_7_out, or_8_out;

  not not_1 (not_1_out, JumpAddress[7]);
  not not_2 (not_2_out, JumpAddress[6]);
  not not_3 (not_3_out, JumpAddress[5]);
  not not_4 (not_4_out, JumpAddress[4]);
  not not_5 (not_5_out, JumpAddress[3]);
  not not_6 (not_6_out, JumpAddress[2]);
  not not_7 (not_7_out, JumpAddress[1]);
  not not_8 (not_8_out, JumpAddress[0]);
  and and_1 (and_1_out, Jump, JumpAddress[0]);
  T_Flip_Flop t_ff_1 (
    .T(1'b1), .clk(clock_1_out), .Q(CurrentAddress[0]), .reset(or_1_out), .preset(and_1_out));  // open: Qn
  or or_1 (or_1_out, and_2_out, Reset);
  Clock #(.highDuration(2), .lowDuration(2)) clock_1 (.out(clock_1_out));
  and and_2 (and_2_out, not_8_out, Jump);
  and and_3 (and_3_out, Jump, JumpAddress[1]);
  T_Flip_Flop t_ff_2 (
    .T(CurrentAddress[0]), .clk(clock_1_out), .Q(CurrentAddress[1]), .reset(or_2_out), .preset(and_3_out));  // open: Qn
  or or_2 (or_2_out, and_4_out, Reset);
  and and_4 (and_4_out, not_7_out, Jump);
  and and_5 (and_5_out, CurrentAddress[1], CurrentAddress[0]);
  and and_6 (and_6_out, Jump, JumpAddress[2]);
  T_Flip_Flop t_ff_3 (
    .T(and_5_out), .clk(clock_1_out), .Q(CurrentAddress[2]), .reset(or_3_out), .preset(and_6_out));  // open: Qn
  or or_3 (or_3_out, and_7_out, Reset);
  and and_7 (and_7_out, not_6_out, Jump);
  and and_8 (and_8_out, CurrentAddress[2], CurrentAddress[1], CurrentAddress[0]);
  and and_9 (and_9_out, Jump, JumpAddress[3]);
  T_Flip_Flop t_ff_4 (
    .T(and_8_out), .clk(clock_1_out), .Q(CurrentAddress[3]), .reset(or_4_out), .preset(and_9_out));  // open: Qn
  or or_4 (or_4_out, and_10_out, Reset);
  and and_10 (and_10_out, not_5_out, Jump);
  and and_11 (and_11_out, CurrentAddress[3], CurrentAddress[2], CurrentAddress[1], CurrentAddress[0]);
  T_Flip_Flop t_ff_5 (
    .T(and_11_out), .clk(clock_1_out), .Q(CurrentAddress[4]), .reset(or_5_out), .preset(and_12_out));  // open: Qn
  and and_12 (and_12_out, Jump, JumpAddress[4]);
  or or_5 (or_5_out, and_13_out, Reset);
  and and_13 (and_13_out, not_4_out, Jump);
  and and_14 (and_14_out, CurrentAddress[4], CurrentAddress[3], CurrentAddress[2], CurrentAddress[1], CurrentAddress[0]);
  and and_15 (and_15_out, Jump, JumpAddress[5]);
  T_Flip_Flop t_ff_6 (
    .T(and_14_out), .clk(clock_1_out), .Q(CurrentAddress[5]), .reset(or_6_out), .preset(and_15_out));  // open: Qn
  or or_6 (or_6_out, and_16_out, Reset);
  and and_16 (and_16_out, not_3_out, Jump);
  and and_17 (and_17_out, CurrentAddress[5], CurrentAddress[4], CurrentAddress[3], CurrentAddress[2], CurrentAddress[1], CurrentAddress[0]);
  and and_18 (and_18_out, Jump, JumpAddress[6]);
  T_Flip_Flop t_ff_7 (
    .T(and_17_out), .clk(clock_1_out), .Q(CurrentAddress[6]), .reset(or_7_out), .preset(and_18_out));  // open: Qn
  or or_7 (or_7_out, and_19_out, Reset);
  and and_19 (and_19_out, not_2_out, Jump);
  and and_20 (and_20_out, CurrentAddress[6], CurrentAddress[5], CurrentAddress[4], CurrentAddress[3], CurrentAddress[2], CurrentAddress[1], CurrentAddress[0]);
  and and_21 (and_21_out, Jump, JumpAddress[7]);
  T_Flip_Flop t_ff_8 (
    .T(and_20_out), .clk(clock_1_out), .Q(CurrentAddress[7]), .reset(or_8_out), .preset(and_21_out));  // open: Qn
  or or_8 (or_8_out, and_22_out, Reset);
  and and_22 (and_22_out, not_1_out, Jump);
endmodule

module ConditionalInterpreter (
  input  [7:0] Reg3,
  input  [7:0] Instruction,
  input  [7:0] Reg0,
  output [7:0] JumpAddress,
  output Jump
);

  wire and_1_out, not_1_out, not_2_out, not_3_out, or_1_out, or_2_out, xor_1_out, xor_2_out, xor_3_out,
       xor_4_out, xor_5_out, xor_6_out, xor_7_out, xor_8_out;

  xor xor_1 (xor_1_out, Reg3[0], 1'b0);
  xor xor_2 (xor_2_out, Reg3[1], 1'b0);
  xor xor_3 (xor_3_out, Reg3[2], 1'b0);
  xor xor_4 (xor_4_out, Reg3[3], 1'b0);
  xor xor_5 (xor_5_out, Reg3[4], 1'b0);
  xor xor_6 (xor_6_out, Reg3[5], 1'b0);
  xor xor_7 (xor_7_out, Reg3[6], 1'b0);
  xor xor_8 (xor_8_out, Reg3[7], 1'b0);
  or or_1 (or_1_out, xor_1_out, xor_2_out, xor_3_out, xor_4_out, xor_5_out, xor_6_out, xor_7_out);
  or or_2 (or_2_out, xor_1_out, xor_2_out, xor_3_out, xor_4_out, xor_5_out, xor_6_out, xor_7_out, xor_8_out);
  and and_1 (and_1_out, or_1_out, ~xor_8_out);  // AND_Gate
  not not_1 (not_1_out, or_2_out);
  not not_2 (not_2_out, and_1_out);
  Multiplexer #(.select(3)) multiplexer_1 (
    .in0(1'b0), .in1(not_1_out), .in2(xor_8_out), .in3(not_2_out), .in4(1'b1), .in5(or_2_out),
    .in6(not_3_out), .in7(and_1_out), .out(Jump), .sel(Instruction[2:0]));
  not not_3 (not_3_out, xor_8_out);

  assign JumpAddress = Reg0;

  // Notes on the sheet:
  //   0 = NEVER
  //   1 = EQUAL TO 0
  //   2 = SMALLER THAN 0
  //   3 = SMALLER OR EQUAL TO 0
  //   4 = ALWAYS
  //   5 = DIFFERENT FROM 0
  //   6 = GREATER OR EQUAL TO 0
  //   7 = GREATER THAN 0
endmodule

module Switch8Bit (
  input  Enable,
  input  [7:0] Data,
  output [7:0] OutputData
);

  and and_1 (OutputData[0], Enable, Data[0]);
  and and_2 (OutputData[1], Enable, Data[1]);
  and and_3 (OutputData[2], Enable, Data[2]);
  and and_4 (OutputData[3], Enable, Data[3]);
  and and_5 (OutputData[4], Enable, Data[4]);
  and and_6 (OutputData[5], Enable, Data[5]);
  and and_7 (OutputData[6], Enable, Data[6]);
  and and_8 (OutputData[7], Enable, Data[7]);
endmodule

module Compute2sComplement (
  input  [7:0] in_1
);

  wire [7:0] not_1_out;

  assign not_1_out = ~in_1;  // NOT_Gate not_1, 8 bits wide
endmodule
